# Fritzing sketch Dash_fritz (saved by Fritzing 0.9.3b)
circuit board: 8.46667cm x 5.64444cm
breadboards: 1

parts:
  J1 = Screw terminal - 2 pins [package=THT]
  J2 = Screw terminal - 2 pins [package=THT]
  JP1 = Header 6 [package=molex-1x6_lock]
  JP2 = Header 6 [package=molex-1x6_lock]
  Part1 = Adafruit LSM9DS1 9DoF Breakout [part_number="Adafruit #3387"]
  Raspberry_Pi1 = Raspberry Pi B+
  U1 = LM386 [package=dip08]  # not connected

nets:
  N1: J1.pin1, JP2.3
  N2: J1.pin2, J2.pin2, JP1.3, JP2.5, Raspberry_Pi1.GND
  N3: J2.pin1, JP2.4
  N4: JP1.1, Part1.SDA, Raspberry_Pi1.GPIO2
  N5: JP1.2, Part1.SCL, Raspberry_Pi1.GPIO3
  3V3: JP1.5, Part1.VIN, Raspberry_Pi1.3v3, Raspberry_Pi1.3V3

notes:
  L. Audio
  R. Audio
  Antenna
  TEA5767
  Digital Dashboard

custom parts:
  Adafruit LSM9DS1 9DoF Breakout: Add motion, direction and orientation sensing to your Arduino project with this all-in-one 9-DOF sensor. Inside the chip are three sensors, one is a classic 3-axis accelerometer, which can tell you which direction is down towards the Earth (by measuring gravity) or how fast the board is accelerating in 3D space. The other is a 3-axis magnetometer that can sense where the strongest magnetic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
