# Fritzing sketch LM386_breadboard (saved by Fritzing 0.9.3b)
circuit board: 8.46667cm x 5.64444cm
breadboards: 1

parts:
  C1 = Electrolytic Capacitor [capacitance=1µF package="100 mil [THT, electrolytic]"]
  C2 = Electrolytic Capacitor [capacitance=1µF package="100 mil [THT, electrolytic]"]
  C3 = Tantalum Capacitor [capacitance=1μF package="100 mil [THT, tantalum]"]
  C4 = Ceramic Capacitor [capacitance=100nF package="100 mil [THT, multilayer]"]
  R1 = Resistor [tolerance=±5% resistance=1.0k package=THT]
  R2 = Resistor [tolerance=±5% resistance=10 package=THT]
  U1 = LM386 [package=dip08]
  C5 = Ceramic Capacitor [capacitance="100 nF" package="0805 [SMD, multilayer]"]
  C6 = Electrolytic Capacitor [capacitance=1µF package="100 mil [THT, electrolytic]"]
  R3 = Resistor [tolerance=±5% resistance=12M package=THT]
  SP1 = SPEAKER [package=pcb_mount_speaker]  # not connected

nets (from the pcb view):
  N1: C1.+, U1.BP
  N2: C2.-, R2.Pin_0
  N3: C2.+, R2.Pin_1, U1.GAIN
  N4: C3.-, U1.V+, R3.Pin_0
  N5: C3.+, R1.Pin_0, R3.Pin_1
  N6: C4.0, U1.OUT, C6.-
  N7: C4.1, R1.Pin_1
  N8: U1.+IN, C5.1
  N9: U1.V-, C6.+

notes:
  12v VCC
  GND
  Mono speaker
  Ouput from pi screw terminal
  12V
